# Fritzing sketch LineFollower (saved by Fritzing 0.9.2b)
breadboards: 1

parts:
  Parte1 = Arduino Uno (Rev3) - ICSP
  U1 = QRD1114 [package=qrd1114]
  U2 = QRD1114 [package=qrd1114]
  R1 = Resistor [tolerance=±5% resistance=220 package="2010 [SMD]"]
  R2 = Resistor [tolerance=±5% resistance=4.7k package="2010 [SMD]"]
  R3 = Resistor [tolerance=±5% resistance=4.7k package="2010 [SMD]"]
  R4 = Resistor [tolerance=±5% resistance=220 package="2010 [SMD]"]

nets:
  N1: Parte1.A0, U2.C, R3.Pin_0
  N2: Parte1.A1, U1.C, R2.Pin_0
  N3: Parte1.5V, R1.Pin_1, R2.Pin_1, R3.Pin_1, R4.Pin_1
  N4: Parte1.GND, U1.E, U1.K, U2.E, U2.K
  N5: U1.A, R1.Pin_0
  N6: U2.A, R4.Pin_0

notes:
  Right Sensor
  Left Sensor
